# Fritzing sketch rocketmodel.pdf (saved by Fritzing 0.9.3b)
breadboards: 1

parts:
  Part1 = Arduino Uno (Rev3)
  Part2 = MicroSD Card Module
  GY1 = GY-521 (MPU-6050) [form="♀ (female)" package=THT]

nets:
  N1: Part1.A4/SDA, GY1.pin4
  N2: Part1.A5/SCL, GY1.pin3
  N3: Part1.D11_PWM/MOSI, Part2.MOSI
  N4: Part1.D12/MISO, Part2.MISO
  N5: Part1.D13/SCK, Part2.SCK
  N6: Part1.D4, Part2.CS
  5V: Part1.5V, Part2.VCC, GY1.pin1
  GND: Part1.GND, Part2.GND, GY1.pin2

custom parts:
  GY-521 (MPU-6050): Placa GY-521 basada en conjunto de acelerómetro+giroscopios MPU-6050
